# Fritzing sketch Semáforo (saved by Fritzing 0.9.3b)
breadboards: 1

parts:
  Componente1 = Arduino Uno (Rev3)
  R1 = Resistor [tolerance=±5% resistance=150 package=THT]
  LED1 = LED - 5mm [color="Red (633nm)" package="5 mm [THT]"]
  LED2 = LED - 5mm [color="Yellow (585nm)" package="5 mm [THT]"]
  LED3 = LED - 5mm [color="Green (555nm)" package="5 mm [THT]"]
  R2 = Resistor [tolerance=±5% resistance=150 package=THT]
  R3 = Resistor [tolerance=±5% resistance=150 package=THT]
  U1 = POT [package=pot_mammoth]

nets:
  N1: Componente1.A5/SCL, U1.A
  N2: Componente1.D2, LED3.anode
  N3: Componente1.D3_PWM, LED2.anode
  N4: Componente1.D4, LED1.anode
  N5: Componente1.5V, U1.E
  N6: Componente1.GND, R1.Pin_0, R2.Pin_0, R3.Pin_0, U1.S
  N7: R1.Pin_1, LED1.cathode
  N8: LED2.cathode, R2.Pin_1
  N9: LED3.cathode, R3.Pin_1
