# Fritzing sketch Dimmer (saved by Fritzing 0.9.3b)
breadboards: 1

parts:
  Componente1 = Arduino Uno (Rev3)
  R1 = Resistor [tolerance=±5% resistance=150 package=THT]
  LED1 = LED - 5mm [color="Red (633nm)" package="5 mm [THT]"]
  U1 = POT [package=pot_mammoth]

nets:
  N1: Componente1.A5/SCL, U1.A
  N2: Componente1.D3_PWM, LED1.anode
  N3: Componente1.5V, U1.E
  N4: Componente1.GND, R1.Pin_0, U1.S
  N5: R1.Pin_1, LED1.cathode
