# Fritzing sketch LED RGB (saved by Fritzing 0.9.3b)
breadboards: 1

parts:
  Componente1 = Arduino Uno (Rev3)
  R1 = Resistor [tolerance=±5% resistance=330 package=THT]
  U1 = POT [package=pot_mammoth]
  LED1 = RGB LED (com. cathode, rgb) [package="5 mm [THT]"]
  U2 = POT [package=pot_mammoth]
  U3 = POT [package=pot_mammoth]
  R2 = Resistor [tolerance=±5% resistance=330 package=THT]
  R3 = Resistor [tolerance=±5% resistance=330 package=THT]

nets:
  N1: Componente1.A0, U3.A
  N2: Componente1.A1, U2.A
  N3: Componente1.A2, U1.A
  N4: Componente1.D3_PWM, R3.Pin_0
  N5: Componente1.D5_PWM, R2.Pin_0
  N6: Componente1.D6_PWM, R1.Pin_0
  N7: Componente1.5V, U1.E, U2.E, U3.E
  N8: Componente1.GND, U1.S, LED1.common_cathode, U2.S, U3.S
  N9: R1.Pin_1, LED1.red_anode
  N10: LED1.green_anode, R2.Pin_1
  N11: LED1.blue_anode, R3.Pin_1
