# Fritzing sketch Buzzer (saved by Fritzing 0.9.3b)
breadboards: 1

parts:
  Componente1 = Arduino Uno (Rev3)
  J1 = Piezo Speaker
  S1 = Pushbutton [package="[THT]"]
  R1 = Resistor [tolerance=±5% resistance=100 package=THT]

nets:
  N1: Componente1.D10_PWM/SS, S1.Pin_1, S1.Pin_2
  N2: Componente1.D11_PWM/MOSI, R1.Pin_0
  N3: Componente1.GND, J1.pin1, S1.Pin_3, S1.Pin_4
  N4: J1.pin2, R1.Pin_1
