# Fritzing sketch D7 (saved by Fritzing 0.9.3b)
breadboards: 1

parts:
  Componente1 = Arduino Uno (Rev3)
  7_Segment1 = 7 Segment Display
  R1 = Resistor [tolerance=±5% resistance=330 package=THT]

nets:
  N1: Componente1.D8, 7_Segment1.Segment_F
  N2: Componente1.D9_PWM, 7_Segment1.Segment_G
  N3: Componente1.D2, 7_Segment1.Segment_E
  N4: Componente1.D3_PWM, 7_Segment1.Segment_D
  N5: Componente1.D4, 7_Segment1.Segment_C
  N6: Componente1.D5_PWM, 7_Segment1.Segment_DP
  N7: Componente1.D6_PWM, 7_Segment1.Segment_B
  N8: Componente1.D7, 7_Segment1.Segment_A
  N9: Componente1.GND, R1.Pin_0
  N10: 7_Segment1.common_anode, R1.Pin_1

notes:
  VSS
  D0
