# Fritzing sketch LCD (saved by Fritzing 0.9.3b)
breadboards: 1

parts:
  Componente1 = Arduino Uno (Rev3)
  LCD1 = LCD screen
  R1 = Resistor [tolerance=±5% resistance=100 package=THT]

nets:
  N1: Componente1.D9_PWM, R1.Pin_0
  N2: Componente1.D2, LCD1.RS
  N3: Componente1.D3_PWM, LCD1.E
  N4: Componente1.D4, LCD1.DB4
  N5: Componente1.D5_PWM, LCD1.DB5
  N6: Componente1.D6_PWM, LCD1.DB6
  N7: Componente1.D7, LCD1.DB7
  5V: Componente1.5V, LCD1.VDD, LCD1.LED+
  GND: Componente1.GND, LCD1.VSS, LCD1.R/W, LCD1.LED-
  N8: LCD1.V0, R1.Pin_1

notes:
  VSS
  VDD
  V0
  RS
  RW
  E
  D0
  D1
  D2
  D3
  D4
  D5
  D6
  D7
  +
  -
