# Fritzing sketch LCD_NTC_Rele (saved by Fritzing 0.9.3b)
breadboards: 1

parts:
  LCD1 = LCD screen
  R2 = Resistor [tolerance=±5% resistance=10k package=THT]
  R3 = Temperature Sensor (Thermistor) [thermistor_type=NTC package=THT]
  OMRON1 = OMRON PCB Power Relay – G5LE [part_number="G5LE-1\n" package=THT]
  Componente1 = Arduino Uno (Rev3) - ICSP
  Componente1_2 = Arduino Uno (Rev3)
  Q1 = NPN-Transistor [package="TO92 [THT]"]
  R4 = Resistor [tolerance=±5% resistance=10k package=THT]
  LED1 = LED - 5mm [color="Red (635nm)" package="5 mm [THT]"]
  R5 = Resistor [tolerance=±5% resistance=330 package=THT]
  R6 = Resistor [tolerance=±5% resistance=100 package=THT]
  LED2 = LED - 5mm [color="White (6500K)" package="5 mm [THT]"]

nets:
  GND: LCD1.VSS, LCD1.R/W, LCD1.LED-, R2.Pin_0, OMRON1.COIL1, OMRON1.C, Componente1.GND, Componente1_2.GND, LED2.anode
  5V: LCD1.VDD, LCD1.LED+, R3.pin_1, Componente1.5V, Componente1_2.5V, Q1.E, R5.Pin_1
  N1: LCD1.V0, R6.Pin_1
  N2: LCD1.RS, Componente1.D2, Componente1_2.D2
  N3: LCD1.E, Componente1.D3_PWM, Componente1_2.D3_PWM
  N4: LCD1.DB4, Componente1.D4, Componente1_2.D4
  N5: LCD1.DB5, Componente1.D5_PWM, Componente1_2.D5_PWM
  N6: LCD1.DB6, Componente1.D6_PWM, Componente1_2.D6_PWM
  N7: LCD1.DB7, Componente1.D7, Componente1_2.D7
  N8: R2.Pin_1, R3.pin_0, Componente1.A5/SCL, Componente1_2.A5/SCL
  N9: OMRON1.COIL2, Q1.C, LED2.cathode
  N10: OMRON1.B, LED1.cathode
  N11: Componente1.D9_PWM, Componente1_2.D9_PWM, R6.Pin_0
  N12: Componente1.D10_PWM/SS, R4.Pin_0
  N13: Q1.B, R4.Pin_1
  N14: LED1.anode, R5.Pin_0

notes:
  VSS
  VDD
  V0
  RS
  RW
  E
  D0
  D1
  D2
  D3
  D4
  D5
  D6
  D7
  +
  -
