# Fritzing sketch MSerial_RX (saved by Fritzing 0.9.3b)
breadboards: 1

parts:
  Componente1 = Arduino Uno (Rev3)
  R2 = Resistor [tolerance=±5% resistance=330 package=THT]
  J1 = Piezo Speaker
  LED1 = RGB LED (com. cathode, rgb) [package="5 mm [THT]"]
  R3 = Resistor [tolerance=±5% resistance=330 package=THT]
  R4 = Resistor [tolerance=±5% resistance=330 package=THT]
  R5 = Resistor [tolerance=±5% resistance=100 package=THT]

nets:
  N1: Componente1.D8, R4.Pin_1
  N2: Componente1.D9_PWM, R3.Pin_0
  N3: Componente1.D10_PWM/SS, R2.Pin_0
  N4: Componente1.D3_PWM, R5.Pin_0
  N5: Componente1.GND, LED1.green_anode
  N6: R2.Pin_1, LED1.red_anode
  N7: J1.pin2, R5.Pin_1
  N8: LED1.common_cathode, R3.Pin_1
  N9: LED1.blue_anode, R4.Pin_0
