# Fritzing sketch MSerial_TX (saved by Fritzing 0.9.3b)
breadboards: 1

parts:
  Componente1 = Arduino Uno (Rev3)
  U1 = POT [package=pot_mammoth]

nets:
  N1: Componente1.A5/SCL, U1.A
  N2: Componente1.5V, U1.E
  N3: Componente1.GND, U1.S
