# Fritzing sketch Blink e botão (saved by Fritzing 0.9.3b)
breadboards: 1

parts:
  Componente1 = Arduino Uno (Rev3)
  R1 = Resistor [tolerance=±5% resistance=150 package=THT]
  LED1 = LED - 5mm [color="Red (633nm)" package="5 mm [THT]"]
  R2 = Resistor [tolerance=±5% resistance=10k package=THT]
  S1 = Pushbutton [package="[THT]"]

nets:
  N1: Componente1.D9_PWM, R2.Pin_1, S1.Pin_3, S1.Pin_4
  N2: Componente1.D13/SCK, LED1.anode
  N3: Componente1.GND, R1.Pin_0, S1.Pin_1, S1.Pin_2
  N4: Componente1.5V, R2.Pin_0
  N5: R1.Pin_1, LED1.cathode
