# Fritzing sketch LDR (saved by Fritzing 0.9.3b)
breadboards: 1

parts:
  Componente1 = Arduino Uno (Rev3)
  R1 = Resistor [tolerance=±5% resistance=150 package=THT]
  LED1 = LED - 5mm [color="Red (633nm)" package="5 mm [THT]"]
  R2 = Resistor [tolerance=±5% resistance=10k package=THT]
  R3 = Photocell (LDR) [package=THT]

nets:
  N1: Componente1.A5/SCL, R2.Pin_1, R3.pin_1
  N2: Componente1.D3_PWM, LED1.anode
  N3: Componente1.5V, R2.Pin_0
  N4: Componente1.GND, R1.Pin_0, R3.pin_0
  N5: R1.Pin_1, LED1.cathode
