# Fritzing sketch Rele (saved by Fritzing 0.9.3b)
breadboards: 1

parts:
  Q1 = NPN-Transistor [package="TO92 [THT]"]
  Componente1 = Arduino Uno (Rev3)
  OMRON1 = OMRON PCB Power Relay – G5LE [part_number="G5LE-1\n" package=THT]
  M1 = DC Motor
  R1 = Resistor [tolerance=±5% resistance=10k package=THT]
  BAT1 = BC9VPC [package=bc9vpc]

nets:
  N1: Q1.E, Componente1.5V
  N2: Q1.B, R1.Pin_0
  N3: Componente1.GND, M1.pin_2, BAT1.V-
  N4: Componente1.D4, R1.Pin_1
  N5: OMRON1.B, M1.pin_1
